# Fritzing sketch jdCobot100_circuit (saved by Fritzing 1.0.2b)

parts:
  부품1 = 16-Channel 12-bit PWM Servo Shield - I2C [part_number=1411]
  J1 = Basic Servo
  J2 = Basic Servo
  J3 = Basic Servo
  J4 = Basic Servo
  J5 = Basic Servo
  VCC1 = 4 x AAA Battery Mount
  OLED1 = OLED 128x64 I2C Monochrome Display GND-VDD

nets:
  N1: 부품1.PWRIN, VCC1.+
  GND: 부품1.GND, J1.gnd, J2.gnd, J3.gnd, J4.gnd, J5.gnd, VCC1.-, OLED1.GND
  N2: 부품1.PWM4, J5.pulse
  VCC: 부품1.5.0V, J1.vcc, J2.vcc, J3.vcc, J4.vcc, J5.vcc
  N3: 부품1.PWM3, J2.pulse
  N4: 부품1.PWM2, J4.pulse
  N5: 부품1.PWM1, J3.pulse
  N6: 부품1.PWM0, J1.pulse
  5V: 부품1.5V, OLED1.VDD
  N7: 부품1.SDA, OLED1.SDA
  N8: 부품1.SCL, OLED1.SCK

notes:
  battery AAx4 6V
  Base Servo 0
  forearm servo 3
  Upperarm servo 2
  Shoulder servo 1
  gripper servo 4
  OLED

custom parts:
  16-Channel 12-bit PWM Servo Shield - I2C: You want to make a cool Arduino robot, maybe a hexapod walker, or maybe just a piece of art with a lot of moving parts. Or maybe you want to drive a lot of LEDs with precise PWM output. This shield is just like our popular PWM/Servo Breakout but now Arduino-ready and works with any Arduino that uses shields: Uno, Leo, Mega, ADK, its all good. Using only two I2C pins, control 16 free-running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
  OLED 128x64 I2C Monochrome Display GND-VDD: OLED 128x64 I2C Monochrome Display. Note: there are two variants of this part, this one is the GND VDD SCK SDA variant. The other is VDD GND SCK SDA. Make sure you select the part that matches your module as using the incorrect part will probably destroy your module! In addition the mounting holes are marked on silkscreen but not by default drilled. If you want drilled mounting holes, copy a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
